# Fritzing sketch Flight Simulator Controller (saved by Fritzing 0.8.3b)
breadboards: 1

parts:
  Part1 = Arduino Uno (Rev3)
  U1 = POT [package=pot_mammoth]
  U2 = POT [package=pot_mammoth]
  U3 = POT [package=pot_mammoth]
  U4 = POT [package=pot_mammoth]

nets:
  N1: Part1.A0, U1.A
  N2: Part1.A1, U2.A
  N3: Part1.A2, U3.A
  N4: Part1.A3, U4.A
  N5: U1.S, U3.S
  N6: U1.E, U2.S, U2.E, U3.E
